# Fritzing sketch user_circuit_diagram (saved by Fritzing 0.9.3b)
breadboards: 1

parts:
  U1 = ESP32S-HiLetgo [part_number=ESP32S-HiLetgo]
  元件1 = Arduino Mega 2560 (Rev3)
  LED1 = LED - 5mm [color="Red (633nm)" package="5 mm [THT]"]
  LED2 = LED - 5mm [color="Yellow (595nm)" package="5 mm [THT]"]
  R1 = Resistor [tolerance=±5% resistance=220 package=THT]
  R2 = Resistor [tolerance=±5% resistance=220 package=THT]
  Keypad4x2 = Keypad Membran 4x4

nets:
  VIN: U1.VIN, 元件1.5V
  N1: U1.GPIO16, 元件1.D18/TX1
  N2: U1.GPIO17, 元件1.D19/RX1
  GND: U1.GND, 元件1.GND, LED1.cathode, LED2.cathode
  N3: 元件1.D11_PWM, Keypad4x2.Pin1
  N4: 元件1.D10_PWM, Keypad4x2.Pin2
  N5: 元件1.D9_PWM, Keypad4x2.Pin3
  N6: 元件1.D8_PWM, Keypad4x2.Pin4
  N7: 元件1.D2_PWM, R1.Pin_0
  N8: 元件1.D3_PWM, R2.Pin_1
  N9: 元件1.D4_PWM, Keypad4x2.Pin8
  N10: 元件1.D5_PWM, Keypad4x2.Pin7
  N11: 元件1.D6_PWM, Keypad4x2.Pin6
  N12: 元件1.D7_PWM, Keypad4x2.Pin5
  N13: LED1.anode, R2.Pin_0
  N14: LED2.anode, R1.Pin_1

custom parts:
  ESP32S-HiLetgo: HiLetgo ESP-WROOM-32 ESP32 ESP-32S Development Board 2.4GHz Dual-Mode WiFi + Bluetooth Dual Cores Microcontroller The ESP32 integrated with Antenna switches, RF Balun, power amplifiers, low-noise amplifiers, filters, and management modules, and the entire solution occupies the least area of PCB. 2.4 GHz Wi-Fi plus Bluetooth dual-mode chip, with TSMC Ultra-low power consumption 40nm technology,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
  Keypad Membran 4x4: Membrane Keypad 4x4 Matrix
